# Fritzing sketch simon (saved by Fritzing 0.8.5b)
breadboards: 1

parts:
  Part1 = Arduino Mega 2560 (Rev3)
  LED1 = LED - 5mm [color="Red (633nm)" package="5 mm [THT]"]
  LED2 = LED - 5mm [color="Red (633nm)" package="5 mm [THT]"]
  LED3 = LED - 5mm [color="Red (633nm)" package="5 mm [THT]"]
  LED4 = LED - 5mm [color="Red (633nm)" package="5 mm [THT]"]
  J1 = Piezo Speaker
  S1 = Toggle Switch [package=THT]
  S2 = Pushbutton [package="[THT]"]
  S3 = Pushbutton [package="[THT]"]
  S4 = Pushbutton [package="[THT]"]
  S5 = Pushbutton [package="[THT]"]
  R1 = Resistor [tolerance=±5% resistance=220 package=THT]
  R2 = Resistor [tolerance=±5% resistance=220 package=THT]
  R3 = Resistor [tolerance=±5% resistance=220 package=THT]
  R4 = Resistor [tolerance=±5% resistance=220 package=THT]
  R5 = Resistor [tolerance=±5% resistance=220 package=THT]
  R6 = Resistor [tolerance=±5% resistance=220 package=THT]
  R7 = Resistor [tolerance=±5% resistance=220 package=THT]
  R8 = Resistor [tolerance=±5% resistance=220 package=THT]
  R10 = Resistor [tolerance=±5% resistance=220 package=THT]
  R11 = Resistor [tolerance=±5% resistance=220 package=THT]

nets:
  N1: Part1.SCL, S3.Pin_1, S3.Pin_2, R5.Pin_1
  N2: Part1.D13_PWM, J1.pin2
  N3: Part1.D12_PWM, R2.Pin_0
  N4: Part1.D9_PWM, R4.Pin_0
  N5: Part1.5V, S1.L2, S2.Pin_3, S2.Pin_4, S3.Pin_3, S3.Pin_4, S4.Pin_3, S4.Pin_4, S5.Pin_3, S5.Pin_4
  N6: Part1.GND, LED3.cathode, LED4.cathode, R1.Pin_0, R3.Pin_1, R5.Pin_0, R6.Pin_0, R10.Pin_0, R11.Pin_0
  N7: Part1.D2_PWM, S1.L1, R1.Pin_1
  N8: Part1.D3_PWM, R7.Pin_0
  N9: Part1.D4_PWM, S5.Pin_1, S5.Pin_2, R10.Pin_1
  N10: Part1.D5_PWM, S4.Pin_1, S4.Pin_2, R11.Pin_1
  N11: Part1.D6_PWM, R8.Pin_0
  N12: LED1.anode, R4.Pin_1
  N13: LED2.anode, R8.Pin_1
  N14: LED3.anode, R7.Pin_1
  N15: LED4.anode, R2.Pin_1
  N16: J1.pin1, R3.Pin_0
  N17: S2.Pin_1, S2.Pin_2, R6.Pin_1
